# Fritzing sketch schematic (saved by Fritzing 0.9.9b)
breadboards: 1

parts:
  part = Arduino Micro (Rev3)
  S1 = SWITCH-MOMENTARY-2 [package=tactile-pth]
  S2 = SWITCH-MOMENTARY-2 [package=tactile-pth]
  S3 = SWITCH-MOMENTARY-2 [package=tactile-pth]
  S4 = SWITCH-MOMENTARY-2 [package=tactile-pth]
  S5 = SWITCH-MOMENTARY-2 [package=tactile-pth]
  Bluetooth_HC-05 = Bluetooth HC-05 Macho

nets:
  GND: part.GND, S1.2, S2.2, S3.2, S4.2, S5.2, Bluetooth_HC-05.GND
  N1: part.D3/SCL, Bluetooth_HC-05.TXD
  N2: part.D4_PWM/A6, Bluetooth_HC-05.RXD
  N3: part.D5_PWM, S1.1
  N4: part.D6_PWM/A7, S2.1
  N5: part.D7, S3.1
  N6: part.D8_PWM/A8, S4.1
  N7: part.D9_PWM/A9, S5.1
  3V3: part.3V3, Bluetooth_HC-05.VCC
